# Fritzing sketch tester (saved by Fritzing 0.8.7b)
breadboards: 1

parts:
  LED1 = LED - 5mm [color="Red (633nm)" package="5 mm [THT]"]
  LED2 = LED - 5mm [color="Red (633nm)" package="5 mm [THT]"]
  LED3 = LED - 5mm [color="Red (633nm)" package="5 mm [THT]"]
  J1 = Piezo Speaker  # not connected
  S1 = Pushbutton [package="[THT]"]
  S2 = Pushbutton [package="[THT]"]
  R1 = Resistor [tolerance=±5% resistance=220 package=THT]
  R2 = Resistor [tolerance=±5% resistance=220 package=THT]
  R3 = Resistor [tolerance=±5% resistance=220 package=THT]
  R4 = Resistor [tolerance=±5% resistance=220 package=THT]
  R5 = Resistor [tolerance=±5% resistance=220 package=THT]
  Raspberry_Pi_1 = Raspberry Pi 3 [part_number=RPI-3-V1.2]  # not connected
  Part1 = Adafruit ADS1115 16Bit I2C ADC [part_number="Adafruit #1085"]  # not connected
  Part2 = INA219 High Side DC Current Sensor Breakout [part_number=904]  # not connected

nets:
  N1: LED1.cathode, R3.Pin_1
  N2: LED1.anode, LED2.anode, LED3.anode, S1.Pin_3, S1.Pin_4, S2.Pin_1, S2.Pin_2, R4.Pin_1, R5.Pin_1
  N3: LED2.cathode, R2.Pin_1
  N4: LED3.cathode, R1.Pin_1
  N5: S1.Pin_1, S1.Pin_2
  N6: S2.Pin_3, S2.Pin_4
  N7: R1.Pin_0, R3.Pin_0
  N8: R2.Pin_0, R4.Pin_0, R5.Pin_0

custom parts:
  Adafruit ADS1115 16Bit I2C ADC: For microcontrollers without an analog-to-digital converter or when you want a higher-precision ADC, the ADS1115 provides 16-bit precision at 860 samples/second over I2C. The chip can be configured as 4 single-ended input channels, or two differential channels. As a nice bonus, it even includes a programmable gain amplifier, up to x16, to help boost up smaller single/differential signals to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
  INA219 High Side DC Current Sensor Breakout: This breakout board will solve all your power-monitoring problems. Instead of struggling with two multimeters, you can just use the handy INA219B chip on this breakout to both measure both the high side voltage and DC current draw over I2C with 1% precision. Most current-measuring devices such as our current panel meter are only good for low side measuring. That means that unless you want to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
